# Fritzing sketch fan_control_board (saved by Fritzing 0.9.3b)
breadboards: 1

parts:
  U1 = NodeMCU V1.0
  S1 = Pushbutton [package="[THT]"]
  DHT1 = DHT22 Humidity and Temperature Sensor
  Q1 = TRANSISTOR_NPN [package=to-92]
  R1 = Resistor [tolerance=±5% resistance=100 package="0603 [SMD]"]
  F1 = Fan - Ventilador [package=THT]
  U2 = Mini-360 DC-DC Buck converter [package=THT]
  BAT1 = BC9VPC [part_number=FAN package=bc9vpc]

nets:
  N1: U1.D2, DHT1.DATA
  3V3: U1.3V3, DHT1.VDD, U2.OUT+
  GND: U1.GND, S1.Pin_1, S1.Pin_2, DHT1.GND, Q1.E, U2.IN-, U2.OUT-, BAT1.V-
  N2: U1.D5, S1.Pin_3, S1.Pin_4
  N3: U1.D6, R1.Pin_0
  N4: Q1.B, R1.Pin_1
  N5: Q1.C, F1.GND
  N6: F1.5V, U2.IN+, BAT1.V+

notes:
  Buck converter for
  e.g. 12V -> 3.3V
  Fan
  Power supply
  e.g. 12V

custom parts:
  NodeMCU V1.0: ESP8266 based NodeMCU
  Fan - Ventilador: Ventilador de 2 pines, se encuentra comunmente en computadoras de escritorio
  Mini-360 DC-DC Buck converter: Mini-360 DC-DC Buck converter. Tiny buck step down voltage converter, input voltage 4.75 to 23V output 1 to 17V adjustable. Available from ebay and the like.
